# Fritzing sketch Схема 2 (saved by Fritzing 0.9.5d)
breadboards: 1

parts:
  Компонент1 = Arduino Nano (Rev3.0)
  Raspberry_Pi_1 = Raspberry Pi 3 [part_number=RPI-3-V1.2]
  IC1 = ULN2003A [package="SO16 [SMD]"]
  U1 = Vibration Motor- ROB-08449 [package=vibe-motor-10mm]

nets:
  N1: Компонент1.D1/TX, IC1.In_1
  N2: Компонент1.GND, IC1.0V
  N3: Компонент1.D2, IC1.In_2
  N4: Компонент1.D3, IC1.In_3
  N5: Компонент1.D4, IC1.In_4
  N6: Компонент1.VIN, Raspberry_Pi_1.GPIO8
  N7: Компонент1.5V, IC1.In_7
  N8: IC1.Out_7, U1.-
  N9: IC1.Out_3, U1.+
