# Fritzing sketch Схема 1 (saved by Fritzing 0.9.5d)
breadboards: 1

parts:
  MD03A1 = Dual VNH2SP30 Motor Driver [part_number=MXI508]
  VCC1 = 4 x AAA Battery Mount
  VCC2 = 4 x AAA Battery Mount
  Компонент1 = SparkFun ESP8266 Thing
  Mod1 = HC-SR04 Ultrasonic Distance Sensor
  U1 = Vibration Motor- ROB-08449 [package=vibe-motor-10mm]
  U2 = Vibration Motor- ROB-08449 [package=vibe-motor-10mm]

nets:
  N1: MD03A1.1INa, Компонент1.GPIO5
  N2: MD03A1.1INb, Компонент1.GPIO4
  N3: MD03A1.GND, VCC2.+
  N4: MD03A1.+5V_(IN), VCC1.+, VCC2.-
  N5: MD03A1.2INb#142, Компонент1.GPIO2
  N6: MD03A1.2INb#143, Компонент1.GPIO0
  N7: MD03A1.OUT_1A, U1.+
  N8: MD03A1.OUT_1B, U1.-
  N9: MD03A1.OUT_2A, U2.+
  N10: MD03A1.OUT_2B, U2.-
  N11: VCC1.-, Компонент1.VIN
  GND: Компонент1.GND, Mod1.GND
  VCC: Компонент1.VCC, Mod1.VCC
  N12: Компонент1.GPIO14, Mod1.ECHO
  N13: Компонент1.GPIO12, Mod1.TRIG

custom parts:
  HC-SR04 Ultrasonic Distance Sensor: The HC-SR04 is an ultrasonic distance sensor. It is capable of providing measurement for ranges of 2cm to 400cm. The module operates at 5V.
